// Logisim project logisimaula1.circ as structural Verilog: 7 circuits, main circuit main
module main (
  input  in_1,
  input  in_2
);

  meiasoma meiasoma_1 (.in_1(in_1), .in_2(in_2));  // open: carry, out
endmodule

module meiasoma (
  input  in_1,
  input  in_2,
  output carry,
  output out
);

  wire not_1_out, or_1_out;

  or or_1 (or_1_out, in_1, in_2);
  and and_1 (carry, in_1, in_2);
  not not_1 (not_1_out, carry);
  and and_2 (out, not_1_out, or_1_out);
endmodule

module somacompleta (
  input  in_1,
  input  in_2,
  input  in_3,
  output out_4,
  output out_5
);

  wire meiasoma_1_carry, meiasoma_1_out, meiasoma_2_carry;

  meiasoma meiasoma_1 (.in_1(in_2), .in_2(in_3), .carry(meiasoma_1_carry), .out(meiasoma_1_out));
  meiasoma meiasoma_2 (.in_1(in_1), .in_2(meiasoma_1_out), .carry(meiasoma_2_carry), .out(out_5));
  or or_1 (out_4, meiasoma_1_carry, meiasoma_2_carry);
endmodule

module soma (
  input  [3:0] in_1,
  input  [3:0] in_2,
  output [3:0] out_3
);

  wire somacompleta_1_out_4, somacompleta_2_out_4, somacompleta_3_out_4;

  // Probe on in_1
  // Probe on in_2
  somacompleta somacompleta_1 (
    .in_1(in_1[0]), .in_2(in_2[0]), .in_3(1'b0), .out_4(somacompleta_1_out_4), .out_5(out_3[0]));
  somacompleta somacompleta_2 (
    .in_1(somacompleta_1_out_4), .in_2(in_1[1]), .in_3(in_2[1]), .out_4(somacompleta_2_out_4),
    .out_5(out_3[1]));
  somacompleta somacompleta_3 (
    .in_1(somacompleta_2_out_4), .in_2(in_1[2]), .in_3(in_2[2]), .out_4(somacompleta_3_out_4),
    .out_5(out_3[2]));
  somacompleta somacompleta_4 (
    .in_1(somacompleta_3_out_4), .in_2(in_1[3]), .in_3(in_2[3]), .out_5(out_3[3]));  // open: out_4
  // Probe on out_3
endmodule

module soma8bits (
  input  [7:0] in_1,
  input  [7:0] in_2,
  output [7:0] out_3
);

  wire somacompleta_1_out_4, somacompleta_2_out_4, somacompleta_3_out_4, somacompleta_4_out_4,
       somacompleta_5_out_4, somacompleta_6_out_4, somacompleta_7_out_4;

  // Probe on in_1
  somacompleta somacompleta_1 (
    .in_1(in_1[0]), .in_2(in_2[0]), .in_3(1'b0), .out_4(somacompleta_1_out_4), .out_5(out_3[0]));
  // Probe on in_2
  somacompleta somacompleta_2 (
    .in_1(somacompleta_1_out_4), .in_2(in_1[1]), .in_3(in_2[1]), .out_4(somacompleta_2_out_4),
    .out_5(out_3[1]));
  somacompleta somacompleta_3 (
    .in_1(somacompleta_2_out_4), .in_2(in_1[2]), .in_3(in_2[2]), .out_4(somacompleta_3_out_4),
    .out_5(out_3[2]));
  // Probe on out_3
  somacompleta somacompleta_4 (
    .in_1(somacompleta_3_out_4), .in_2(in_1[3]), .in_3(in_2[3]), .out_4(somacompleta_4_out_4),
    .out_5(out_3[3]));
  somacompleta somacompleta_5 (
    .in_1(somacompleta_4_out_4), .in_2(in_1[4]), .in_3(in_2[4]), .out_4(somacompleta_5_out_4),
    .out_5(out_3[4]));
  somacompleta somacompleta_6 (
    .in_1(somacompleta_5_out_4), .in_2(in_1[5]), .in_3(in_2[5]), .out_4(somacompleta_6_out_4),
    .out_5(out_3[5]));
  somacompleta somacompleta_7 (
    .in_1(somacompleta_6_out_4), .in_2(in_1[6]), .in_3(in_2[6]), .out_4(somacompleta_7_out_4),
    .out_5(out_3[6]));
  somacompleta somacompleta_8 (
    .in_1(somacompleta_7_out_4), .in_2(in_1[7]), .in_3(in_2[7]), .out_5(out_3[7]));  // open: out_4

  // Other names for the same wires on the sheet: _1A = in_1[0]; _2A = in_1[1]; _3A = in_1[2]; _4A = in_1[3];
  //   _5A = in_1[4]; _6A = in_1[5]; _7A = in_1[6]; _8A = in_1[7]; _1B = in_2[0]; _2B = in_2[1]; _3B = in_2[2];
  //   _4B = in_2[3]; _5B = in_2[4]; _6B = in_2[5]; _7B = in_2[6]; _8B = in_2[7]; _1C = out_3[0]; _2C = out_3[1];
  //   _3C = out_3[2]; _4C = out_3[3]; _5C = out_3[4]; _6C = out_3[5]; _7C = out_3[6]; _8C = out_3[7]
endmodule

module ula (
  input  [7:0] in_1,
  input  [7:0] in_2,
  output [7:0] out_3,
  output [1:0] out_4
);

  wire [7:0] and_1_out, or_1_out, soma8bits_1_out_3;

  assign and_1_out = in_1 & in_2;  // AND_Gate and_1, 8 bits wide
  assign or_1_out = in_1 | in_2;  // OR_Gate or_1, 8 bits wide
  soma8bits soma8bits_1 (.in_1(in_1), .in_2(in_2), .out_3(soma8bits_1_out_3));
  Multiplexer #(.select(2), .width(8)) multiplexer_1 (
    .in0(soma8bits_1_out_3), .in2(and_1_out), .in3(or_1_out), .out(out_3), .sel(out_4));  // open: in1, en

  // Other names for the same wires on the sheet: A[7:0] = in_1; B[7:0] = in_2
endmodule

module multiplicador (
  input  [7:0] in_1,
  input  [7:0] in_2,
  output [7:0] out_3
);

  // Probe on in_1
  // Probe on in_2
  // Probe on out_3

  // Other names for the same wires on the sheet: _1A = in_1[0]; _2A = in_1[1]; _3A = in_1[2]; _4A = in_1[3];
  //   _5A = in_1[4]; _6A = in_1[5]; _7A = in_1[6]; _8A = in_1[7]; _1B = in_2[0]; _2B = in_2[1]; _3B = in_2[2];
  //   _4B = in_2[3]; _5B = in_2[4]; _6B = in_2[5]; _7B = in_2[6]; _8B = in_2[7]; _1C = out_3[0]; _2C = out_3[1];
  //   _3C = out_3[2]; _4C = out_3[3]; _5C = out_3[4]; _6C = out_3[5]; _7C = out_3[6]; _8C = out_3[7]
endmodule
